# Fritzing sketch Neopixel for GassistPi (saved by Fritzing 0.9.3b)
breadboards: 1

parts:
  Raspberry_Pi_1 = Raspberry Pi 3 [part_number=RPI-3-V1.2]
  WeMos_D1_Mini1 = WeMos D1 Mini
  Part1 = 12 NeoPixel Ring [part_number=1643]

nets:
  N1: Raspberry_Pi_1.GIPO27, WeMos_D1_Mini1.D2
  N2: Raspberry_Pi_1.GIPO24, WeMos_D1_Mini1.D3
  GND: Raspberry_Pi_1.GND, WeMos_D1_Mini1.G, Part1.GND
  5V: Raspberry_Pi_1.5V, WeMos_D1_Mini1.5V
  3V3: WeMos_D1_Mini1.3V3, Part1.VDD
  N3: WeMos_D1_Mini1.D4, Part1.IN

custom parts:
  12 NeoPixel Ring: 12 ultra bright smart LED NeoPixels are arranged in a circle with 1.5" (37mm) outer diameter. The rings are 'chainable' - connect the output pin of one to the input pin of another. Use only one microcontroller pin to control as many as you can chain together! Each LED is addressable as the driver chip is inside the LED. Each one has ~18mA constant current drive so the color will be very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
